# Fritzing sketch water_pump_sketch (saved by Fritzing 0.9.3b)
perfboards: 1

parts:
  U9 = PIC-ICSP [package=molex-1x6]
  U10 = PIC-ICSP [package=molex-1x6]
  U11 = PIC-ICSP [package=molex-1x6]
  U12 = PIC-ICSP [package=molex-1x6]
  U13 = PIC-ICSP [package=molex-1x6]
  U14 = PIC-ICSP [package=molex-1x6]
  J2 = Power Jack [package=power_jack_smd]
  U15 = Mini-360 DC-DC Buck converter [package=THT]
  부품4 = FC-28 Soil Hygrometer Module
  부품5 = FC-28 Soil Hygrometer Module - Probe
  Relay_5V2 = Keyes Relay [package=THT]
  U1 = NodeMCU V3.0

nets:
  N1: U9.PGM, 부품4.AO, U1.A0
  N2: U9.PGC, U1.GND#41
  N3: U9.PGD, U1.VU
  N4: U9.GND, U1.S3
  N5: U9.VCC, U1.S2
  N6: U9.VPP, U1.S1
  N7: U10.PGM, U1.D0
  N8: U10.PGC, U1.D1
  N9: U10.PGD, U1.D2
  N10: U10.GND, U1.D3
  N11: U10.VCC, U1.D4
  VCC: U10.VPP, U12.VCC, U13.PGD, U1.3V3
  N12: U11.PGM, U12.GND, U13.PGC, U14.PGC, U1.GND#6, U1.GND#13, U1.GND#16, U1.GND#33
  N13: U11.PGC, Relay_5V2.signal, U1.D5
  N14: U11.PGD, 부품4.VCC, U1.D6
  N15: U11.GND, U1.D7
  N16: U11.VCC, U1.D8
  N17: U11.VPP, U1.RX
  N18: U12.PGM, U1.SC
  N19: U12.PGC, U1.S0
  N20: U12.PGD, U1.SK
  N21: U12.VPP, U1.EN
  N22: U13.PGM, U1.TX
  N23: U14.PGM, U1.RST
  N24: U14.PGD, U15.OUT+, Relay_5V2.power, U1.Vin
  N25: J2.GND, U15.IN+, Relay_5V2.C
  N26: J2.GNDBREAK, U15.IN-
  N27: U15.OUT-, Relay_5V2.ground
  N28: 부품4.POS, 부품5.POS
  N29: 부품4.NEG, 부품5.NEG

notes:
  pump

custom parts:
  Mini-360 DC-DC Buck converter: Mini-360 DC-DC Buck converter. Tiny buck step down voltage converter, input voltage 4.75 to 23V output 1 to 17V adjustable. Available from ebay and the like.
  FC-28 Soil Hygrometer Module: The FC-28 is a soil hygrometer module that uses the Texas Instruments LM393 comparator chip to provide an analog measurement of soil humidity. The digital output is high when soil moisture is over a certain threshold, as determined by adjusting the potentiometer.
  FC-28 Soil Hygrometer Module - Probe: The FC-28 is a soil hygrometer module that uses the Texas Instruments LM393 comparator chip to provide an analog measurement of soil humidity.
  Keyes Relay: The Keyes 5V relay module is suitable for SCM development, home appliance control. It uses a 5V~12V TIL control signal which can control DC / AC signal.
  NodeMCU V3.0: ESP8266 based NodeMCU
